// Logisim project lab2.circ as structural Verilog: 1 circuit, main circuit main
module main (
);

  wire clock_1_out, clock_2_out, clock_3_out, clock_4_out, clock_5_out, clock_6_out, nand_1_out, nand_2_out,
       nand_3_out, nand_4_out, nand_5_out, nand_6_out, nand_7_out, nand_8_out, nand_9_out, nand_10_out,
       nand_11_out, nand_12_out, nand_13_out, nand_14_out, nand_15_out, nand_16_out, nand_17_out,
       nand_18_out, nand_19_out, nand_20_out, nor_1_out, nor_2_out, undriven, undriven_2, undriven_3,
       undriven_4, undriven_5, undriven_6, undriven_7;

  nand nand_1 (nand_1_out, undriven, undriven_5);
  nand nand_2 (nand_2_out, undriven_5, undriven_2);
  nor nor_1 (nor_1_out, undriven_6, nor_2_out);
  nor nor_2 (nor_2_out, nor_1_out, undriven_7);
  nand nand_3 (nand_3_out, undriven_3, nand_4_out);
  nand nand_4 (nand_4_out, nand_3_out, undriven_4);
  nand nand_5 (nand_5_out, nand_1_out, nand_6_out);
  nand nand_6 (nand_6_out, nand_5_out, nand_2_out);
  Clock #(.highDuration(2), .lowDuration(2)) clock_1 (.out(clock_1_out));
  Clock clock_2 (.out(clock_2_out));
  Clock #(.highDuration(2), .lowDuration(2)) clock_3 (.out(clock_3_out));
  Clock clock_4 (.out(clock_4_out));
  Clock #(.highDuration(2), .lowDuration(2)) clock_5 (.out(clock_5_out));
  Clock clock_6 (.out(clock_6_out));
  nand nand_7 (nand_7_out, clock_1_out, clock_1_out);
  nand nand_8 (nand_8_out, nand_7_out, clock_2_out);
  nand nand_9 (nand_9_out, clock_3_out, nand_10_out);
  nand nand_10 (nand_10_out, clock_4_out, clock_4_out);
  nand nand_11 (nand_11_out, clock_5_out, clock_5_out);
  nand nand_12 (nand_12_out, clock_6_out, clock_6_out);
  nand nand_13 (nand_13_out, clock_5_out, nand_12_out);
  nand nand_14 (nand_14_out, nand_11_out, clock_6_out);
  nand nand_15 (nand_15_out, nand_7_out, nand_16_out);
  nand nand_16 (nand_16_out, nand_15_out, nand_8_out);
  nand nand_17 (nand_17_out, nand_9_out, nand_18_out);
  nand nand_18 (nand_18_out, nand_17_out, nand_10_out);
  nand nand_19 (nand_19_out, nand_13_out, nand_20_out);
  nand nand_20 (nand_20_out, nand_19_out, nand_14_out);
  LED led_1 (.in(nand_15_out));
  LED led_2 (.in(nand_16_out));
  LED led_3 (.in(nand_17_out));
  LED led_4 (.in(nand_18_out));
  LED led_5 (.in(nand_19_out));
  LED led_6 (.in(nand_20_out));

  // Notes on the sheet:
  //   S
  //   R
  //   S
  //   C
  //   R
  //   R
  //   S
  //   Асинхронный RS триггер с прямыми входами (2 элемента ИЛИ-НЕ)
  //   Асинхронный RS триггер с инверсными входами (2 элемента И-НЕ)
  //   Синхронный RS триггер
  //   Q
  //   !Q
  //   Q
  //   !Q
  //   Q
  //   !Q
  //   S
  //   R
  //   S
  //   R
  //   S
  //   R
  //   Модификации RS тригера
  //   S-тригер
  //   R-тригер
  //   E-тригер
  //   Q
  //   !Q
  //   Q
  //   !Q
  //   Q
  //   !Q
endmodule
